# Fritzing sketch Overview (saved by Fritzing 0.9.3b)

parts:
  Part1 = Arduino Uno (Rev3) - ICSP
  S1 = H-Bridge with L298N
  S2 = H-Bridge with L298N
  S3 = H-Bridge with L298N
  S4 = H-Bridge with L298N
  J1 = Basic Servo
  J2 = Basic Servo
  M1 = DC Motor
  M2 = DC Motor
  M3 = DC Motor
  M4 = DC Motor
  M5 = Stepper Motor - Bipolar
  M6 = Stepper Motor - Bipolar
  Power_plug1 = Power plug
  ENCODER = female pin header, 4 pins [form="♀ (female)"]
  I2C = female pin header, 4 pins [form="♀ (female)"]

nets:
  N1: Part1.A1, S3.IN1
  N2: Part1.A4/SDA, I2C.pin2
  N3: Part1.A5/SCL, I2C.pin1
  N4: Part1.ICSP_MISO, Part1.D12/MISO, S1.IN4
  GND: Part1.GND, S1.GND, S2.GND, S3.GND, S4.GND, J1.gnd, J2.gnd, Power_plug1.GND, ENCODER.pin2, I2C.pin4
  N5: Part1.D8, S1.IN2, S2.IN3, S3.IN3, S4.IN2
  N6: Part1.D9_PWM, J1.pulse
  N7: Part1.D10_PWM/SS, J2.pulse
  N8: Part1.D13/SCK, S1.IN3
  N9: Part1.D2, ENCODER.pin3
  N10: Part1.D3_PWM, ENCODER.pin4
  N11: Part1.D4, S3.IN2
  N12: Part1.D6_PWM, S1.ENA, S2.ENB, S3.ENB, S4.ENA
  N13: Part1.D7, S1.IN1, S2.IN4, S3.IN4, S4.IN1
  N14: Part1.5V, ENCODER.pin1, I2C.pin3
  12V: Part1.VIN, S1.12V, S2.12V, S3.12V, S4.12V, Power_plug1.VCC
  5V: S1.5V, J1.vcc
  N15: S1.ENB, S1.ENB-5V
  N16: S1.M1-01, M2.pin_2
  N17: S1.M1-02, M2.pin_1
  N18: S1.M2-01, M6.C
  N19: S1.M2-02, M5.D
  N20: S2.M2-01, M1.pin_2
  N21: S2.M2-02, M1.pin_1
  5V_2: S3.5V, J2.vcc
  N22: S3.ENA, S3.ENA-5V
  N23: S3.M1-01, M6.B
  N24: S3.M1-02, M5.A
  N25: S3.M2-01, M3.pin_2
  N26: S3.M2-02, M3.pin_1
  N27: S4.M1-01, M4.pin_2
  N28: S4.M1-02, M4.pin_1

custom parts:
  H-Bridge with L298N: h-bridge
